# Fritzing sketch URocket (saved by Fritzing 0.9.3b)
circuit board: 4.98556cm x 5.36263cm

parts:
  ESP32 = ESP32S-HiLetgo [part_number=ESP32S-HiLetgo]
  MPU6050 = MPU-6050 Board GY-521 [form="♀ (female)" package=THT]
  BMP280 = Adafruit_BMP280

nets:
  N1: ESP32.3.3, MPU6050.pin1, BMP280.3.3V
  GND: ESP32.GND, MPU6050.pin2, BMP280.GND
  N2: ESP32.GPIO21, MPU6050.pin4, BMP280.SDO/ADR
  N3: ESP32.GPIO22, MPU6050.pin3, BMP280.SCK/SCL

custom parts:
  ESP32S-HiLetgo: HiLetgo ESP-WROOM-32 ESP32 ESP-32S Development Board 2.4GHz Dual-Mode WiFi + Bluetooth Dual Cores Microcontroller The ESP32 integrated with Antenna switches, RF Balun, power amplifiers, low-noise amplifiers, filters, and management modules, and the entire solution occupies the least area of PCB. 2.4 GHz Wi-Fi plus Bluetooth dual-mode chip, with TSMC Ultra-low power consumption 40nm technology,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
  MPU-6050 Board GY-521: Acelerometro y Giroscopio MPU-6050 Board GY-521
  Adafruit_BMP280: Bosch has stepped up their game with their new BMP280 sensor, an environmental sensor with temperature, barometric pressure that is the next generation upgrade to the BMP085/BMP180/BMP183. This sensor is great for all sorts of weather sensing and can even be used in both I2C and SPI! This precision sensor from Bosch is the best low-cost, precision sensing solution for measuring barometric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
